# Fritzing sketch fritzing (saved by Fritzing 0.9.3b)
breadboards: 1

parts:
  Part1 = RFID-RC522-v3
  Part2 = Photon
  Grove1 = Grove OLED 128x96
  R1 = Resistor [tolerance=±5% resistance=10k package="0402 [SMD]"]
  R2 = Resistor [tolerance=±5% resistance=6.8k package="0402 [SMD]"]

nets:
  N1: Part1.SDA, Part2.A2
  N2: Part1.SCK, Part2.A3
  N3: Part1.MOSI, Part2.A5
  N4: Part1.MISO, Part2.A4
  N5: Part1.RST, Part2.DAC
  3.3V: Part1.3.3V, Part2.3V3
  GND: Part2.GND, Grove1.GND
  VIN: Part2.VIN, Grove1.VCC, R1.Pin_0, R2.Pin_0
  N6: Part2.D0, Grove1.SDA, R1.Pin_1
  N7: Part2.D1, Grove1.SCL, R2.Pin_1

custom parts:
  RFID-RC522-v3: A simple China made RFID-RC522 Reader (6x4 cm); do check the pin labels, as this is a MFRC522 based clone.
